# Fritzing sketch Final (saved by Fritzing 0.9.3b)
breadboards: 1

parts:
  Composant1 = Arduino Uno (Rev3)
  R1 = Resistor [tolerance=±5% resistance=100 package=THT]
  L1 = Inductor [package="400 mil [THT]"]
  R2 = Resistor [tolerance=±5% resistance=1M package=THT]
  R3 = Resistor [tolerance=±5% resistance=150 package=THT]
  R4 = Resistor [tolerance=±5% resistance=180 package=THT]
  R5 = Resistor [tolerance=±5% resistance=150 package=THT]
  ROUGE = LED - 5mm [color="Red (633nm)" package="5 mm [THT]"]
  JAUNE = LED - 5mm [color="Yellow (592nm)" package="5 mm [THT]"]
  VERT = LED - 5mm [color="Green (560nm)" package="5 mm [THT]"]

nets (from the schematic view):
  Patate: Composant1.A0, R1.Pin_1, L1.pin_1
  N1: Composant1.D9_PWM, R1.Pin_0
  N2: Composant1.GND, R2.Pin_1, ROUGE.cathode, JAUNE.cathode, VERT.cathode
  N3: Composant1.D3_PWM, R4.Pin_0
  N4: Composant1.D5_PWM, R5.Pin_0
  N5: Composant1.D7, R3.Pin_0
  N6: L1.pin_0, R2.Pin_0
  N7: R3.Pin_1, VERT.anode
  N8: R4.Pin_1, ROUGE.anode
  N9: R5.Pin_1, JAUNE.anode

notes:
  Patate
